// Logisim project IT012_Lab02_25521288.circ as structural Verilog: 8 circuits, main circuit FA
module FA (
  input  A,
  input  B,
  input  Cin,
  output S,
  output Cout
);

  wire AND_1_out, AND_2_out, XOR_1_out;

  xor XOR_1 (XOR_1_out, A, B);
  and AND_1 (AND_1_out, A, B);
  and AND_2 (AND_2_out, XOR_1_out, Cin);
  xor XOR_2 (S, XOR_1_out, Cin);
  or or_1 (Cout, AND_1_out, AND_2_out);
endmodule

module ADDSUB4 (
  input  [3:0] A,
  input  [3:0] B,
  input  SUB,
  output [3:0] S,
  output C
);

  wire FA0_cout, FA1_cout, FA2_cout, xor_1_out, xor_2_out, xor_3_out, xor_4_out;

  xor xor_1 (xor_1_out, SUB, B[0]);
  xor xor_2 (xor_2_out, SUB, B[1]);
  xor xor_3 (xor_3_out, SUB, B[2]);
  xor xor_4 (xor_4_out, SUB, B[3]);
  FA FA0 (.A(SUB), .B(A[0]), .Cin(xor_1_out), .S(S[0]), .Cout(FA0_cout));
  FA FA1 (.A(FA0_cout), .B(A[1]), .Cin(xor_2_out), .S(S[1]), .Cout(FA1_cout));
  // Probe on FA1_cout
  FA FA2 (.A(FA1_cout), .B(A[2]), .Cin(xor_3_out), .S(S[2]), .Cout(FA2_cout));
  // Probe on FA2_cout
  FA FA3 (.A(FA2_cout), .B(A[3]), .Cin(xor_4_out), .S(S[3]), .Cout(C));
  // Probe on FA0_cout
endmodule

module ALU8 (
  input  [2:0] OP,
  input  [7:0] A,
  input  [7:0] B,
  output [7:0] R,
  output Z,
  output LT
);

  wire [7:0] adder_1_out, adder_2_out, and_1_out, multiplexer_1_out, multiplexer_2_out, not_1_out, or_1_out,
       subtractor_1_out, subtractor_2_out, xor_1_out;

  Adder adder_1 (.a(A), .b(B), .out(adder_1_out));  // open: cin, cout
  Adder adder_2 (.a(A), .b(8'h1), .out(adder_2_out));  // open: cin, cout
  Subtractor subtractor_1 (.a(A), .b(B), .out(subtractor_1_out));  // open: bin, bout
  Subtractor subtractor_2 (.a(A), .b(8'h1), .out(subtractor_2_out));  // open: bin, bout
  assign and_1_out = A & B;  // AND_Gate and_1, 8 bits wide
  assign or_1_out = A | B;  // OR_Gate or_1, 8 bits wide
  assign not_1_out = ~A;  // NOT_Gate not_1, 8 bits wide
  assign xor_1_out = A ^ B;  // XOR_Gate xor_1, 8 bits wide
  Multiplexer #(.select(2), .width(8)) multiplexer_1 (
    .in0(adder_1_out), .in1(adder_2_out), .in2(subtractor_1_out), .in3(subtractor_2_out),
    .out(multiplexer_1_out), .sel(OP[1:0]));  // open: en
  Multiplexer #(.select(2), .width(8)) multiplexer_2 (
    .in0(and_1_out), .in1(or_1_out), .in2(not_1_out), .in3(xor_1_out), .out(multiplexer_2_out), .sel(OP[1:0]));  // open: en
  LT lt_1 (.A7(A[7]), .B7(B[7]), .R7(subtractor_1_out[7]), .LT(LT));
  Multiplexer #(.width(8)) multiplexer_3 (
    .in0(multiplexer_1_out), .in1(multiplexer_2_out), .out(R), .sel(OP[2]));  // open: en
  nor nor_1 (Z, R[0], R[1], R[2], R[3], R[4], R[5], R[6], R[7]);
endmodule

module DLATCH (
  input  E,
  input  D,
  output Q
);

  Multiplexer multiplexer_1 (.in0(D), .in1(Q), .out(Q), .sel(E));  // open: en
endmodule

module LT (
  input  A7,
  input  B7,
  input  R7,
  output LT
);

  wire and_1_out, and_2_out, and_3_out, not_1_out;

  not not_1 (not_1_out, B7);
  and and_1 (and_1_out, A7, not_1_out);
  and and_2 (and_2_out, not_1_out, R7);
  and and_3 (and_3_out, A7, R7);
  or or_1 (LT, and_1_out, and_2_out, and_3_out);
endmodule

module TN3 (
  input  D,
  output Q1,
  output Q2,
  output Q1_2,
  output Q2_2
);

  wire clock_1_out, d_ff_2_q, dlatch_2_q;

  Clock clock_1 (.out(clock_1_out));
  DLATCH DLATCH (.D(D), .E(clock_1_out), .Q(Q1));
  D_Flip_Flop d_ff_1 (.clk(clock_1_out), .D(D), .Q(Q2));  // open: Qn, preset, en, reset
  DLATCH dlatch_2 (.D(D), .E(clock_1_out), .Q(dlatch_2_q));
  D_Flip_Flop d_ff_2 (.clk(clock_1_out), .D(D), .Q(d_ff_2_q));  // open: Qn, preset, en, reset
  DLATCH dlatch_3 (.D(dlatch_2_q), .E(clock_1_out), .Q(Q1_2));
  D_Flip_Flop d_ff_3 (.clk(clock_1_out), .D(d_ff_2_q), .Q(Q2_2));  // open: Qn, preset, en, reset
endmodule

module REGFILE (
  input  [1:0] RA,
  input  [7:0] DIN,
  input  WE,
  input  [1:0] RB,
  input  [1:0] RD,
  input  in_6,
  output [7:0] R0,
  output [7:0] R1,
  output [7:0] QA,
  output [7:0] QB,
  output [7:0] R2,
  output [7:0] R3
);

  wire and_1_out, decoder_1_out0, decoder_1_out1, decoder_1_out2, decoder_1_out3;

  Decoder #(.select(2)) decoder_1 (
    .out0(decoder_1_out0), .out1(decoder_1_out1), .out2(decoder_1_out2), .out3(decoder_1_out3), .sel(RD),
    .en(WE));
  Register register_1 (.D(DIN), .en(decoder_1_out0), .Q(R0), .clk(and_1_out));  // open: clr
  Register register_2 (.D(DIN), .en(decoder_1_out1), .Q(R1), .clk(and_1_out));  // open: clr
  Register register_3 (.D(DIN), .en(decoder_1_out2), .Q(R2), .clk(and_1_out));  // open: clr
  Register register_4 (.D(DIN), .en(decoder_1_out3), .Q(R3), .clk(and_1_out));  // open: clr
  and and_1 (and_1_out, WE, in_6);
  Multiplexer #(.select(2), .width(8)) multiplexer_1 (
    .in0(R0), .in1(R1), .in2(R2), .in3(R3), .out(QA), .sel(RA));  // open: en
  Multiplexer #(.select(2), .width(8)) multiplexer_2 (
    .in0(R0), .in1(R1), .in2(R2), .in3(R3), .out(QB), .sel(RB));  // open: en
endmodule

module DATAPATH (
  input  SRC,
  input  [1:0] RA,
  input  [2:0] OP,
  input  WE,
  input  [7:0] IMM,
  input  [1:0] RD,
  input  [1:0] RB,
  output [7:0] R0,
  output [7:0] R1,
  output [7:0] R,
  output Z,
  output [7:0] R2,
  output [7:0] R3
);

  wire clock_1_out;
  wire [7:0] multiplexer_1_out, regfile_1_qa, regfile_1_qb;

  REGFILE regfile_1 (
    .DIN(multiplexer_1_out), .WE(WE), .RD(RD), .R0(R0), .R1(R1), .RA(RA), .in_6(clock_1_out), .R2(R2),
    .R3(R3), .RB(RB), .QA(regfile_1_qa), .QB(regfile_1_qb));
  Clock clock_1 (.out(clock_1_out));
  ALU8 alu8_1 (.OP(OP), .A(regfile_1_qa), .B(regfile_1_qb), .R(R), .Z(Z));  // open: LT
  Multiplexer #(.width(8)) multiplexer_1 (.in0(R), .in1(IMM), .out(multiplexer_1_out), .sel(SRC));  // open: en
endmodule
