// Logisim project TN1.circ as structural Verilog
module Warmup (
  input  A,
  input  B,
  output F
);

  wire not_1_out;

  not not_1 (not_1_out, B);
  and and_1 (F, A, not_1_out);
endmodule

module TN1 (
  input  A,
  input  B,
  input  C,
  output NOT,
  output AND,
  output OR,
  output NAND,
  output NOR,
  output XOR,
  output XNOR,
  output XOR3,
  output NAND3,
  output CHAIN
);

  wire nand_2_out;

  xor xor_1 (XOR3, A, B, C);
  nand nand_1 (NAND3, A, B, C);
  nand nand_2 (nand_2_out, A, B);
  not not_1 (NOT, A);
  and and_1 (AND, A, B);
  or or_1 (OR, A, B);
  nand nand_3 (NAND, A, B);
  nor nor_1 (NOR, A, B);
  xor xor_2 (XOR, A, B);
  xnor xnor_1 (XNOR, A, B);
  nand nand_4 (CHAIN, nand_2_out, C);
endmodule
