// Logisim project TN3.circ as structural Verilog: 1 circuit, main circuit main
module main (
  input  A,
  input  B,
  input  C,
  input  D,
  output F
);

  wire A_prime_B_prime_CD_out, A_prime_B_prime_CD_prime_out, A_prime_BC_prime_D_out, A_prime_BCD_out,
       AB_prime_CD_out, ABC_prime_D_out, not_1_out, not_2_out, not_3_out, not_4_out;

  not not_1 (not_1_out, A);
  not not_2 (not_2_out, B);
  not not_3 (not_3_out, C);
  not not_4 (not_4_out, D);
  and A_prime_B_prime_CD_prime (A_prime_B_prime_CD_prime_out, not_1_out, not_2_out, C, not_4_out);
  and A_prime_B_prime_CD (A_prime_B_prime_CD_out, not_1_out, not_2_out, C, D);
  and A_prime_BC_prime_D (A_prime_BC_prime_D_out, not_1_out, B, not_3_out, D);
  and A_prime_BCD (A_prime_BCD_out, not_1_out, B, C, D);
  and AB_prime_CD (AB_prime_CD_out, A, not_2_out, C, D);
  and ABC_prime_D (ABC_prime_D_out, A, B, not_3_out, D);
  or or_1 (F, A_prime_B_prime_CD_prime_out, A_prime_B_prime_CD_out, A_prime_BC_prime_D_out, A_prime_BCD_out, AB_prime_CD_out, ABC_prime_D_out);
endmodule
