// Logisim project TN4.circ as structural Verilog: 1 circuit, main circuit main
module main (
  input  A,
  input  B,
  input  C,
  input  D,
  output EQ1,
  output EQ2
);

  wire A_prime_B_prime_C_out, A_prime_B_prime_C_prime_out, A_prime_B_prime_CD_out,
       A_prime_B_prime_CD_prime_out, A_prime_BC_prime_D_out, A_prime_BCD_out, A_prime_BD_out, A_prime_D_out,
       AB_prime_CD_out, ABC_prime_D_out, B_C_out, B_prime_CD_out, B_prime_D_out, BC_prime_D_out, F_can_out,
       F_pos_out, F_sop_out, not_1_out, not_2_out, not_3_out, not_4_out;

  not not_1 (not_1_out, A);
  not not_2 (not_2_out, B);
  not not_3 (not_3_out, C);
  not not_4 (not_4_out, D);
  and A_prime_B_prime_CD_prime (A_prime_B_prime_CD_prime_out, not_1_out, not_2_out, C, not_4_out);
  and A_prime_B_prime_CD (A_prime_B_prime_CD_out, not_1_out, not_2_out, C, D);
  and A_prime_BC_prime_D (A_prime_BC_prime_D_out, not_1_out, B, not_3_out, D);
  and A_prime_BCD (A_prime_BCD_out, not_1_out, B, C, D);
  and AB_prime_CD (AB_prime_CD_out, A, not_2_out, C, D);
  and ABC_prime_D (ABC_prime_D_out, A, B, not_3_out, D);
  and A_prime_B_prime_C (A_prime_B_prime_C_out, not_1_out, not_2_out, C);
  and A_prime_BD (A_prime_BD_out, not_1_out, B, D);
  and B_prime_CD (B_prime_CD_out, not_2_out, C, D);
  and BC_prime_D (BC_prime_D_out, B, not_3_out, D);
  or B_C (B_C_out, B, C);
  or B_prime_D (B_prime_D_out, not_2_out, D);
  or A_prime_D (A_prime_D_out, not_1_out, D);
  or A_prime_B_prime_C_prime (A_prime_B_prime_C_prime_out, not_1_out, not_2_out, not_3_out);
  or F_can (F_can_out, A_prime_B_prime_CD_prime_out, A_prime_B_prime_CD_out, A_prime_BC_prime_D_out, A_prime_BCD_out, AB_prime_CD_out, ABC_prime_D_out);
  or F_sop (F_sop_out, A_prime_B_prime_C_out, A_prime_BD_out, B_prime_CD_out, BC_prime_D_out);
  and F_pos (F_pos_out, B_C_out, B_prime_D_out, A_prime_D_out, A_prime_B_prime_C_prime_out);
  xnor xnor_1 (EQ1, F_can_out, F_sop_out);
  xnor xnor_2 (EQ2, F_can_out, F_pos_out);
endmodule
